# Fritzing sketch ServoTest Sketch (saved by Fritzing 0.9.10b)
breadboards: 1

parts:
  Pot1 = TRIMPOT [maximum_resistance=10kΩ knob_status=50% power=0.5W package=trimpot_pth_s3_lock]
  NodeMCU1 = Amica NodeMCU DEVKIT 1.0
  IC1_Level_Shifter = 74AHCT125 [part_number=SN74AHCT125 package=dil14]
  ServoL = Basic Servo
  ServoR = Basic Servo
  C1 = Electrolytic Capacitor [capacitance=1000µF voltage=25V package="300 mil [THT, electrolytic]"]

nets:
  GND: Pot1.CCW, NodeMCU1.pin2, NodeMCU1.pin_9, NodeMCU1.pin_25, NodeMCU1.pin_29, IC1_Level_Shifter.1OE, IC1_Level_Shifter.2OE, IC1_Level_Shifter.GND, ServoL.gnd, ServoR.gnd, C1.-
  N1: Pot1.WIPER, NodeMCU1.pin_16
  N2: Pot1.CW, NodeMCU1.pin1, NodeMCU1.pin_10, NodeMCU1.pin_26
  N3: NodeMCU1.pin_13, IC1_Level_Shifter.2A
  N4: NodeMCU1.pin_14, IC1_Level_Shifter.1A
  VCC: NodeMCU1.pin_30, IC1_Level_Shifter.VCC, ServoL.vcc, ServoR.vcc, C1.+
  N5: IC1_Level_Shifter.1Y, ServoL.pulse
  N6: IC1_Level_Shifter.2Y, ServoR.pulse

custom parts:
  74AHCT125: Quad Level-Shifter (3V to 5V) Quadruple Bus Buffer Gates With 3-State Outputs
